# Fritzing sketch ESP32-Zero-RFM95W (saved by Fritzing 1.0.1rc)
circuit board: 2.93855cm x 3.24866cm
breadboards: 1

parts:
  A1 = Waveshare esp32-c3-zero smd
  RFM95W1 = RFM95W LoRa Module
  J2 = male pin header, 6 pins [form="♂ (male)"]
  J1 = male pin header, 6 pins [form="♂ (male)"]
  J3 = male pin header, 2 pins [form="♂ (male)"]
  Pad1 = Pad [width=1.5 height=2 connect=center]
  Pad2 = Pad [width=1.5 height=2 connect=center]

nets:
  N1: A1.Pin_1, J1.pin1
  N2: A1.Pin_2, RFM95W1.1_GND, J1.pin2
  N3: A1.Pin_3, RFM95W1.13_3.3V, J1.pin3
  N4: A1.Pin_4, J1.pin4
  N5: A1.Pin_5, J1.pin5
  N6: A1.Pin_6, J1.pin6
  N7: A1.Pin_7, RFM95W1.14_DIO0
  N8: A1.Pin_8, RFM95W1.4_SCK
  N9: A1.Pin_9, RFM95W1.2_MISO
  N10: A1.Pin_10, RFM95W1.3_MOSI
  N11: A1.Pin_11, RFM95W1.5_NSS_(CS)
  N12: A1.Pin_12, RFM95W1.6_RESET
  N13: A1.Pin_13, J2.pin6
  N14: A1.Pin_14, J2.pin5
  N15: A1.Pin_15, J2.pin4
  N16: A1.Pin_16, J2.pin3, Pad2.pad
  N17: A1.Pin_17, J2.pin2
  N18: A1.Pin_18, J2.pin1
  N19: RFM95W1.9_ANT, J3.pin1, J3.pin2
  N20: RFM95W1.15_DIO1, Pad1.pad

notes:
  ESP32-Zero-RFM95W v1.0

custom parts:
  Waveshare esp32-c3-zero smd: ESP32-C3 Mini Development Board, Based on ESP32-C3FN4 Single-core Processor, 160MHz Running Frequency, 2.4GHz Wi-Fi&Bluetooth 5.
  RFM95W LoRa Module: RF Transceiver by Hope RF. Well supported Arduino libraries are available. This Low Power Long Range Transceiver Module for the frequencies 868MHz and 915MHz and it is also available in other versions.
