# Fritzing sketch RFM95W (saved by Fritzing 1.0.1rc)
circuit board: 2.18986cm x 2.46128cm
breadboards: 1

parts:
  RFM95W1 = RFM95W LoRa Module
  J1 = male pin header, 8 pins [form="♂ (male)"]
  J2 = male pin header, 8 pins [form="♂ (male)"]

nets:
  N1: RFM95W1.1_GND, J2.pin8
  N2: RFM95W1.2_MISO, J2.pin7
  N3: RFM95W1.3_MOSI, J2.pin6
  N4: RFM95W1.4_SCK, J2.pin5
  N5: RFM95W1.5_NSS_(CS), J1.pin5
  N6: RFM95W1.6_RESET, J1.pin6
  N7: RFM95W1.7_DIO5, J1.pin7
  N8: RFM95W1.8_GND, J1.pin8
  N9: RFM95W1.9_ANT, J1.pin1
  N10: RFM95W1.10_GND, J1.pin2
  N11: RFM95W1.11_DIO3, J1.pin3
  N12: RFM95W1.12_DIO4, J1.pin4
  N13: RFM95W1.13_3.3V, J2.pin4
  N14: RFM95W1.14_DIO0, J2.pin3
  N15: RFM95W1.15_DIO1, J2.pin2
  N16: RFM95W1.16_DIO2, J2.pin1

notes:
  Rev 1.1
  GND
  RST
  DIO5
  MISO
  MOSI
  SCK
  3.3V
  DIO0
  DIO1
  DIO2
  NSS
  DIO4
  DIO3
  ANT

custom parts:
  RFM95W LoRa Module: RF Transceiver by Hope RF. Well supported Arduino libraries are available. This Low Power Long Range Transceiver Module for the frequencies 868MHz and 915MHz and it is also available in other versions.
